# Fritzing sketch Semáforo (saved by Fritzing 0.9.3b)
breadboards: 1

parts:
  S1 = Pushbutton [package=THT]
  R1 = Resistor [tolerance=±5% resistance=1k package=THT]
  Componente1 = Arduino Uno (Rev3) - ICSP
  LED1 = LED - 3mm [color="Red (633nm)" package="3 mm [THT]"]
  LED2 = LED - 3mm [color="Yellow (595nm)" package="3 mm [THT]"]
  LED3 = LED - 3mm [color="Green (570nm)" package="3 mm [THT]"]
  LED4 = LED - 3mm [color="Green (565nm)" package="3 mm [THT]"]
  LED5 = LED - 3mm [color="Red (633nm)" package="3 mm [THT]"]
  R2 = Resistor [tolerance=±5% resistance=220 package=THT]
  R3 = Resistor [tolerance=±5% resistance=220 package=THT]
  R4 = Resistor [tolerance=±5% resistance=220 package=THT]
  R5 = Resistor [tolerance=±5% resistance=220 package=THT]
  R6 = Resistor [tolerance=±5% resistance=220 package=THT]
  U1 = POT [package=pot_alpha_rv16af-20]
  J1 = Piezo Speaker

nets:
  N1: S1.leg0, Componente1.GND, LED1.cathode, LED2.cathode, LED3.cathode, LED4.cathode, LED5.cathode, U1.E, J1.pin1
  N2: S1.leg1, R1.Pin_0, Componente1.D2
  N3: R1.Pin_1, Componente1.5V, R2.Pin_1, R3.Pin_1, R4.Pin_1, R5.Pin_1, R6.Pin_1, U1.A
  N4: Componente1.A0, U1.S
  N5: Componente1.D8, J1.pin2
  N6: Componente1.D3_PWM, LED5.anode, R4.Pin_0
  N7: Componente1.D4, LED4.anode, R2.Pin_0
  N8: Componente1.D5_PWM, LED1.anode, R5.Pin_0
  N9: Componente1.D6_PWM, LED2.anode, R6.Pin_0
  N10: Componente1.D7, LED3.anode, R3.Pin_0
